# Fritzing sketch ssd1306 (saved by Fritzing 0.9.3b)

parts:
  MCU1 = Raspberry Pi Zero
  Part2 = OLED Monochrome 128x32 I2C [part_number=931]

nets:
  N1: MCU1.pin_1, Part2.VIN
  N2: MCU1.pin_3, Part2.SDA
  N3: MCU1.pin_5, Part2.SCL
  N4: MCU1.pin_6, MCU1.pin_9, Part2.GND

custom parts:
  OLED Monochrome 128x32 I2C: These displays are small, only about 1" diagonal, but very readable due to the high contrast of an OLED display. This display is made of 128x32 individual white OLED pixels, each one is turned on or off by the controller chip. Because the display makes its own light, no backlight is required. This reduces the power required to run the OLED and is why the display has such high contrast; we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
