# Fritzing sketch mcp-3xxx (saved by Fritzing 0.9.3b)
breadboards: 1

parts:
  MCU1 = Raspberry Pi Zero
  IC1 = MCP3008 8-channel 10-bit ADC [part_number=MCP3008]
  U1 = TMP36 [package=to-92]
  R1 = Rotary Potentiometer (Small) [maximum_resistance=100kΩ package=THT]

nets:
  N1: MCU1.pin_1, MCU1.pin_2, MCU1.pin_3, MCU1.pin_4, IC1.no_name_yet#15, IC1.no_name_yet#16, U1.VCC, R1.leg2
  N2: MCU1.pin_5, MCU1.pin_6, MCU1.pin_8, MCU1.pin_9, MCU1.pin_19, MCU1.pin_20, MCU1.pin_23, MCU1.pin_25, MCU1.pin_30, MCU1.pin_34, IC1.no_name_yet#9, IC1.no_name_yet#11, IC1.no_name_yet#13, IC1.no_name_yet#14, U1.GND, R1.leg1
  N3: MCU1.pin_21, MCU1.pin_22, IC1.no_name_yet#12
  N4: MCU1.pin_24, MCU1.pin_26, IC1.no_name_yet#10
  N5: IC1.no_name_yet#1, U1.VOUT
  N6: IC1.no_name_yet#3, R1.wiper
