# Fritzing sketch pi-dht-input (saved by Fritzing 0.9.4)
breadboards: 1

parts:
  MCU1 = Raspberry Pi Zero
  RHT1 = Humidity and Temperature Sensor RHT03

nets:
  N1: MCU1.pin_2, RHT1.Vcc
  N2: MCU1.pin_6, RHT1.GND_2
  N3: MCU1.pin_7, RHT1.Data-signal
