# Fritzing sketch pi-gpio-input (saved by Fritzing 0.9.3b)
breadboards: 1

parts:
  MCU1 = Raspberry Pi Zero
  S1 = Pushbutton [package="[THT]"]
  R1 = Resistor [tolerance=±5% resistance=220 package="1206 [SMD]"]
  LED1 = smd LED [color="Red (633nm)" package="0603 [SMD]"]

nets:
  N1: MCU1.pin_1, MCU1.pin_3, S1.Pin_1, S1.Pin_2
  N2: MCU1.pin_6, MCU1.pin_39, LED1.cathode
  N3: MCU1.pin_11, R1.Pin_0
  N4: MCU1.pin_12, S1.Pin_3, S1.Pin_4
  N5: R1.Pin_1, LED1.anode
