# Fritzing sketch pi-rotary-encoder (saved by Fritzing 0.9.3b)
breadboards: 1

parts:
  MCU1 = Raspberry Pi Zero
  ENCODER1 = Rotary Encoder with Knob

nets:
  N1: MCU1.pin_25, MCU1.pin_30, ENCODER1.no_name_yet#2
  N2: MCU1.pin_29, ENCODER1.no_name_yet#3
  N3: MCU1.pin_31, ENCODER1.no_name_yet#1

custom parts:
  Rotary Encoder with Knob: Rotary Encoder with 1/4" Shaft and Knob
